# Fritzing sketch finale (saved by Fritzing 0.9.3b)
breadboards: 1

parts:
  U1 = LuaNode32 / ESP32 [part_number=ESP32S-PIN30]
  IC1 = L293D [package=THT]
  M1 = DC Motor
  LDR = KY-018 Photoresistor Module [package="Breakout board"]
  FRONT_ULTRASONIC_SENSOR = hc-sr04
  RGB_LED = KY-016 RGB Full Color LED Module [package="Breakout board"]
  BUZZER = Piezo Speaker
  LCD = LCD1602-I2C
  Mod3 = KY-019 5V Relay Module [package="Breakout board"]
  IR_RECEIVER = KY-022 Infrared Receiver Module [package="Breakout board"]
  DOOR_ULTRASONIC_SENSOR = hc-sr04

nets:
  N1: U1.D34, LDR.S
  VIN: U1.D32, U1.D33, U1.Vin, U1.RX2, U1.TX2, IC1.+Vmotor, IC1.+V, LDR.Vin, FRONT_ULTRASONIC_SENSOR.Trig, Mod3.+, DOOR_ULTRASONIC_SENSOR.Trig
  N2: U1.D25, RGB_LED.G
  N3: U1.D26, IC1.In_2
  N4: U1.D27, IC1.In_1
  N5: U1.D14, IC1.Enable_1
  N6: U1.D13, RGB_LED.R
  3V3: U1.3V3, LCD.VCC, IR_RECEIVER.Vin
  N7: U1.D4, IR_RECEIVER.S
  N8: U1.D18, Mod3.S
  N9: U1.D19, BUZZER.pin1
  N10: U1.D21, LCD.SDA
  N11: U1.D22, LCD.SCL
  N12: U1.D23, RGB_LED.B
  N13: IC1.Out_1_(_Controlled_by_Enable_1_), M1.pin_1
  N14: IC1.Out_2_(_Controlled_by_Enable_1_), M1.pin_2
  GND: BUZZER.pin2, LCD.GND

custom parts:
  LuaNode32 / ESP32: New Image for LuaNode32 DOIT ESP32 DEVKIT V1. Base parts from LuaNode32 / ESP32 ESP32 based LuaNode32 by G.Noorlander DOIT Esp32 DevKit v1 (30 pins long, 11 pins width) by Werner Rothschopf (modified by vanepp Dec 2018)
  KY-018 Photoresistor Module: KY-018 Photoresistor module, used to measure light intensity. It can determine the presence or absence of light.
  KY-016 RGB Full Color LED Module: KY-016 Arduino full color 5mm RGB LED, different colors can be obtained by mixing the three primary colors.
  LCD1602-I2C: A standard character display, usually with 2x16 characters. Comes in many colors with LCM1602 IIC attached.
  KY-019 5V Relay Module: KY-019 5V Relay module, used to control AC circuits. (Special thanks to vanepp for fixing the PCB holes and other errors)
  KY-022 Infrared Receiver Module: KY-022 IR receiver module, reacts to 38kHz infrared light.
